// Logisim project dec_74ls138.circ as structural Verilog: 1 circuit, main circuit main
module main (
  input  x,
  input  y,
  input  z,
  output f
);

  wire m0, m1, m2, m3, m4, m5, m6, m7, nx, ny, nz, y0, y1, y2, y3, y4, y5, y6, y7;

  not not_1 (nx, x);
  not not_2 (ny, y);
  not not_3 (nz, z);
  and and_1 (m0, nx, ny, nz);
  and and_2 (m1, nx, ny, z);
  and and_3 (m2, nx, y, nz);
  and and_4 (m3, nx, y, z);
  and and_5 (m4, x, ny, nz);
  and and_6 (m5, x, ny, z);
  and and_7 (m6, x, y, nz);
  and and_8 (m7, x, y, z);
  not not_4 (y0, m0);
  // Probe on y0
  not not_5 (y1, m1);
  // Probe on y1
  not not_6 (y2, m2);
  // Probe on y2
  not not_7 (y3, m3);
  // Probe on y3
  not not_8 (y4, m4);
  // Probe on y4
  not not_9 (y5, m5);
  // Probe on y5
  not not_10 (y6, m6);
  // Probe on y6
  not not_11 (y7, m7);
  // Probe on y7
  or or_1 (f, m0, m2, m5, m7);
endmodule
